# Fritzing sketch Spear (saved by Fritzing 0.9.3b)
breadboards: 1

parts:
  Componente1 = Arduino Mega 2560 (Rev3)
  R1 = Photocell (LDR) [package=THT]
  S4 = Pushbutton [package="[THT]"]
  LCD1 = LCD screen
  R2 = Rotary Potentiometer (Small) [maximum_resistance=100kΩ package=THT]
  Componente2 = Adafruit Motor/Stepper/Servo Shield [part_number="Adafruit #1438"]
  KEYPAD1 = Membrane Matrix Keypad
  Componente5 = Adafruit TSL2591 [part_number="Adafruit #1980"]
  IR1 = TSOP312.., 314.. [package=THT]  # not connected
  Componente6 = Adafruit DS1307 RTC Breakout [part_number="Adafruit #264"]
  M1 = Stepper Motor - Bipolar
  JACK1 = 2.1mm Barrel Jack with Terminal Block
  R3 = Resistor [tolerance=±10% resistance=330 package="2512 [SMD]"]
  R3_2 = Resistor [tolerance=±10% resistance=330 package="2010 [SMD]"]
  J1 = Piezo Speaker
  R5 = Resistor [tolerance=±5% resistance=220 package=THT]
  S5 = Pushbutton [package="[THT]"]
  R6 = Resistor [tolerance=±5% resistance=220 package=THT]
  S6 = Pushbutton [package="[THT]"]
  R7 = Resistor [tolerance=±5% resistance=220 package=THT]
  S7 = Pushbutton [package="[THT]"]
  R8 = Resistor [tolerance=±5% resistance=220 package=THT]
  S8 = Pushbutton [package="[THT]"]
  R9 = Resistor [tolerance=±5% resistance=220 package=THT]

nets:
  N1: Componente1.A9, R1.pin_0, R3.Pin_0, R3_2.Pin_0
  N2: Componente1.D21/SCL, Componente2.AD5/SCL, Componente5.SCL, Componente6.SCL
  N3: Componente1.D20/SDA, Componente2.AD4/SDA, Componente5.SDA, Componente6.SDA
  N4: Componente1.D13_PWM, LCD1.DB7
  N5: Componente1.D12_PWM, LCD1.DB6
  N6: Componente1.D11_PWM, LCD1.DB5
  N7: Componente1.D10_PWM, LCD1.DB4
  N8: Componente1.D9_PWM, LCD1.E
  N9: Componente1.D8_PWM, LCD1.RS
  GND: Componente1.GND, LCD1.VSS, LCD1.R/W, LCD1.LED-, R2.leg1, Componente5.GND, Componente6.GND, R3.Pin_1, R3_2.Pin_1, J1.pin1, R5.Pin_1, R6.Pin_1, R7.Pin_1, R8.Pin_1, R9.Pin_1
  VIN: Componente1.VIN, R1.pin_1, S4.Pin_3, S4.Pin_4, LCD1.VDD, LCD1.LED+, R2.leg2, Componente5.VIN, Componente6.VCC, S5.Pin_3, S5.Pin_4, S6.Pin_3, S6.Pin_4, S7.Pin_3, S7.Pin_4, S8.Pin_3, S8.Pin_4
  N10: Componente1.D3_PWM, S8.Pin_1, S8.Pin_2, R9.Pin_0
  N11: Componente1.D4_PWM, S7.Pin_1, S7.Pin_2, R8.Pin_0
  N12: Componente1.D5_PWM, S6.Pin_1, S6.Pin_2, R7.Pin_0
  N13: Componente1.D6_PWM, S5.Pin_1, S5.Pin_2, R6.Pin_0
  N14: Componente1.D7_PWM, S4.Pin_1, S4.Pin_2, R5.Pin_0
  N15: Componente1.D32, KEYPAD1.7
  N16: Componente1.D33, KEYPAD1.6
  N17: Componente1.D34, KEYPAD1.5
  N18: Componente1.D35, KEYPAD1.4
  N19: Componente1.D36, KEYPAD1.3
  N20: Componente1.D37, KEYPAD1.2
  N21: Componente1.D38, KEYPAD1.1
  N22: Componente1.D46, J1.pin2
  N23: LCD1.V0, R2.wiper
  N24: Componente2.M3A, M1.D
  N25: Componente2.M3B, M1.B
  N26: Componente2.M4B, M1.C
  N27: Componente2.M4A, M1.A
  N28: Componente2.GND, JACK1.POS
  N29: Componente2.VMOTOR, JACK1.NEG

custom parts:
  Adafruit Motor/Stepper/Servo Shield: The original Adafruit Motorshield kit is one of our most beloved kits, which is why we decided to make something even better. We have upgraded the shield kit to make the bestest, easiest way to drive DC and Stepper motors. This shield will make quick work of your next robotics project! We kept the ability to drive up to 4 DC motors or 2 stepper motors, but added many improvements: Instead of a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
  Membrane Matrix Keypad: Membrane Matrix 3x4 Keypad
  Adafruit TSL2591: When the future is dazzlingly-bright, this ultra-high-range luminosity sensor will help you measure it. The TSL2591 luminosity sensor is an advanced digital light sensor, ideal for use in a wide range of light situations. Compared to low cost CdS cells, this sensor is more precise, allowing for exact lux calculations and can be configured for different gain/timing ranges to detect light ranges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
  Adafruit DS1307 RTC Breakout: This is a great battery-backed real time clock (RTC) that allows your microcontroller project to keep track of time even if it is reprogrammed, or if the power is lost. Perfect for datalogging, clock-building, time stamping, timers and alarms, etc. The DS1307 is the most popular RTC - but it requires 5V power to work (although we've used it with 5V power and 3.3V logic successfully) PCB &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
